# Fritzing sketch tricolorLEDProtoBoardLayout (saved by Fritzing 0.9.4)
breadboards: 1

parts:
  Teensy_v3_2 = Teensy 3.1  # not connected
  Tri-Colour_LED = RGB LED (com. cathode, rgb) [package="5 mm [THT]"]
  220-Ohm_Resistor_(Blue) = Resistor [tolerance=±5% resistance=220 package="2512 [SMD]"]
  220-Ohm_Resistor_(Red) = Resistor [tolerance=±5% resistance=220 package="2512 [SMD]"]
  220-Ohm_Resistor_(Green) = Resistor [tolerance=±5% resistance=220 package="2512 [SMD]"]
  220-Ohm_Resistor_(Green)1 = Resistor [tolerance=±5% resistance=220 package="2512 [SMD]"]
  S1 = Pushbutton [package="[THT]"]

nets:
  N1: Tri-Colour_LED.red_anode, 220-Ohm_Resistor_(Green).Pin_1
  N2: Tri-Colour_LED.common_cathode, 220-Ohm_Resistor_(Green)1.Pin_1
  N3: Tri-Colour_LED.green_anode, 220-Ohm_Resistor_(Blue).Pin_1
  N4: Tri-Colour_LED.blue_anode, 220-Ohm_Resistor_(Red).Pin_1
  N5: 220-Ohm_Resistor_(Green)1.Pin_0, S1.Pin_1, S1.Pin_2
  N6: S1.Pin_3, S1.Pin_4

notes:
  CST8227 - Interfacing
  Lab 03 - PWM
  Tri-colour LED: Red, Green, Blue (RGB)
  Interfacing Lab week 3 by Aria Gomes
  040878659
