# Fritzing sketch My Week4 Breadboard (saved by Fritzing 0.9.4)
breadboards: 1

parts:
  Teensy_3_1 = Teensy 3.1  # not connected
  R1 = Resistor [tolerance=±5% resistance=220 package="1206 [SMD]"]
  R2 = Resistor [tolerance=±5% resistance=220 package="1206 [SMD]"]
  R3 = Resistor [tolerance=±5% resistance=220 package="1206 [SMD]"]
  LED1 = RGB LED (com. cathode, rgb) [package="5 mm [THT]"]
  S1 = Pushbutton [package="[THT]"]
  S2 = Pushbutton [package="[THT]"]
  R4 = Resistor [tolerance=±5% resistance=220 package=THT]

nets:
  N1: R1.Pin_1, LED1.green_anode
  N2: R2.Pin_1, LED1.red_anode
  N3: R3.Pin_1, LED1.blue_anode
  N4: LED1.common_cathode, S1.Pin_1, S1.Pin_2, S2.Pin_1, S2.Pin_2, R4.Pin_0
  N5: S1.Pin_3, S1.Pin_4
  N6: S2.Pin_3, S2.Pin_4, R4.Pin_1

notes:
  CST8227 – Interfacing Lab 04 – Pushbuttons to Control LED Colors Control a tri-color RGB with two switches and a pull-up resistor.
  Side note: I could not find the small PBS so just pretend the ones i used are the smaller ones included in our kit :)
  @Aria Gomes (040878659)
