# Fritzing sketch Bread Board Week 6 (saved by Fritzing 0.9.4)
breadboards: 1

parts:
  LED1 = RGB LED (com. cathode, rgb) [package="5 mm [THT]"]
  Teensy_3_1 = Teensy 3.1  # not connected
  R1 = Resistor [tolerance=±5% resistance=220 package="0805 [SMD]"]
  R2 = Resistor [tolerance=±5% resistance=220 package="0805 [SMD]"]
  R3 = Resistor [tolerance=±5% resistance=220 package="0805 [SMD]"]
  R4 = Temperature Sensor (Thermistor) [thermistor_type=NTC package=THT]
  R5 = TRIMPOT [package=trim_pot_pth]  # not connected
  R7 = Resistor [tolerance=±5% resistance=330 package=THT]

nets:
  N1: LED1.red_anode, R3.Pin_0
  N2: LED1.common_cathode, R2.Pin_0
  N3: LED1.green_anode, R7.Pin_1
  N4: LED1.blue_anode, R1.Pin_0
  N5: R4.pin_0, R4.pin_1, R7.Pin_0

notes:
  CST8227 – Interfacing Lab 06 – User Controlled LED Color
  Use a potentiometer as user input to control the LED color.
  @author Aria Gomes(040878659)
